# Fritzing sketch RogueRouter_Fritzing (saved by Fritzing 0.9.10b)

parts:
  Bauteil1 = SparkFun ESP8266 Thing
  microSD_Transflash1 = SparkFun - microSD Transflash
  ANT1 = Antenna  # not connected
  U1 = LIPO-2000mAh [package=lipo-2000]  # not connected
  Bauteil2 = Sunny Buddy MPPT LiPo Charger  # not connected

nets:
  GND: Bauteil1.GND, microSD_Transflash1.GND
  VCC: Bauteil1.VCC, microSD_Transflash1.VCC
  N1: Bauteil1.GPIO14, microSD_Transflash1.SCK
  N2: Bauteil1.GPIO13, microSD_Transflash1.DI
  N3: Bauteil1.GPIO12, microSD_Transflash1.DO
  N4: Bauteil1.GPIO15, microSD_Transflash1.CS

custom parts:
  Sunny Buddy MPPT LiPo Charger: Switch-mode MPPT charger for single cell LiPo batteries. Accepts up to 20V solar cell input.
